// Logisim project RSC.circ as structural Verilog: 10 circuits, main circuit Logic_U
// LU
module Logic_U (
  input  [31:0] A,
  input  [31:0] B,
  input  S1,
  input  S0,
  output [31:0] Logic_Out
);

  wire [31:0] and_1_out, not_1_out, or_1_out, shifter_1_out;

  // Probe on A
  assign not_1_out = ~A;  // NOT_Gate not_1, 32 bits wide
  // Probe on B
  assign and_1_out = A & B;  // AND_Gate and_1, 32 bits wide
  assign or_1_out = B | A;  // OR_Gate or_1, 32 bits wide
  Shifter #(.width(32), .shift("ar")) shifter_1 (.in(A), .\dist (5'b00001), .out(shifter_1_out));
  Multiplexer #(.select(2), .width(32), .enable("false")) multiplexer_1 (
    .in0(and_1_out), .in1(or_1_out), .in2(shifter_1_out), .in3(not_1_out), .out(Logic_Out), .sel({S1, S0}));
  // Probe on Logic_Out

  // Notes on the sheet:
  //   CLA5
  //   10/14/2022
  //   Brandon Sandoval and Anees Alawmleh
  //   Create an Logic Unit
endmodule

module ALU (
  input  [31:0] A,
  input  [31:0] B,
  input  S2,
  input  S1,
  input  S0,
  output [31:0] ALU_Out
);

  wire [31:0] arith_u_1_au_out, logic_u_1_logic_out;

  // Probe on A
  // Probe on B
  Arith_U arith_u_1 (.A(A), .B(B), .S1(S1), .S0(S0), .AU_out(arith_u_1_au_out));
  Logic_U logic_u_1 (.A(A), .B(B), .S1(S1), .S0(S0), .Logic_Out(logic_u_1_logic_out));
  Multiplexer #(.width(32), .enable("false")) multiplexer_1 (
    .in0(arith_u_1_au_out), .in1(logic_u_1_logic_out), .out(ALU_Out), .sel(S2));
  // Probe on ALU_Out

  // Notes on the sheet:
  //   CLA5
  //   10/14/2022
  //   Create an ALU 
  //   Brandon Sandoval and Anees Alawmleh
endmodule

// AU
module Arith_U (
  input  [31:0] A,
  input  [31:0] B,
  input  S1,
  input  S0,
  output [31:0] AU_out
);

  wire and_1_out, xnor_1_out;
  wire [31:0] adder_1_out, multiplexer_1_out, not_1_out;

  // Probe on A
  // Probe on B
  assign not_1_out = ~B;  // NOT_Gate not_1, 32 bits wide
  Multiplexer #(.select(2), .width(32), .enable("false")) multiplexer_1 (
    .in0(not_1_out), .in1(B), .in2(32'h1), .out(multiplexer_1_out), .sel({S1, S0}));  // open: in3
  Adder #(.width(32)) adder_1 (.a(A), .b(multiplexer_1_out), .out(adder_1_out), .cin(xnor_1_out));  // open: cout
  xnor xnor_1 (xnor_1_out, S0, S1);
  and and_1 (and_1_out, S1, S0);
  Multiplexer #(.width(32), .enable("false")) multiplexer_2 (.in0(adder_1_out), .in1(B), .out(AU_out), .sel(and_1_out));
  // Probe on AU_out

  // Notes on the sheet:
  //   CLA4
  //   9/30/2022
  //   Brandon Sandoval and Anees Alawmleh
  //   Create an Arithmetic Unit
endmodule

module RSC (
);

  wire control_1_acc_bus, control_1_acc_clr, control_1_acc_ld, control_1_ar_ld, control_1_dr_bus,
       control_1_dr_ld, control_1_ir_ld, control_1_outr_ld, control_1_pc_bus, control_1_pc_inc,
       control_1_pc_ld, control_1_r_bus, control_1_r_ld, control_1_ram_en, control_1_ram_r_prime_w,
       control_1_z_ld, Primary_Clock_out, z_reg_1_z_out;
  wire [2:0] control_1_alu_s;
  wire [3:0] outr_1_output;
  wire [31:0] acc_1_output, alu_1_alu_out, ar_1_output, dr_1_output, ir_1_output, r_1_bus_out;
  wire [31:4] outr_1_output_2;

  Clock Primary_Clock (.out(Primary_Clock_out));
  AR ar_1 (.Input(r_1_bus_out), .Clock(Primary_Clock_out), .Load(control_1_ar_ld), .Output(ar_1_output));
  R r_1 (
    .Input(r_1_bus_out), .Clock(Primary_Clock_out), .Load(control_1_r_ld), .Bus(control_1_r_bus),
    .Bus_out(r_1_bus_out));  // open: Output
  ALU alu_1 (
    .A(acc_1_output), .B(r_1_bus_out), .S2(control_1_alu_s[2]), .S1(control_1_alu_s[1]),
    .S0(control_1_alu_s[0]), .ALU_Out(alu_1_alu_out));
  DR dr_1 (
    .Input(r_1_bus_out), .Clock(Primary_Clock_out), .Load(control_1_dr_ld), .Bus(control_1_dr_bus),
    .Output(dr_1_output), .Bus_out(r_1_bus_out));
  OUTR outr_1 (
    .Input(r_1_bus_out), .Clock(Primary_Clock_out), .Load(control_1_outr_ld),
    .Output({outr_1_output_2, outr_1_output}));
  RAM #(.addrWidth(16), .dataWidth(32)) ram_1 (
    .addr(ar_1_output[15:0]), .data(r_1_bus_out), .sel(control_1_ram_en), .clk(Primary_Clock_out),
    .ld(control_1_ram_r_prime_w));  // open: clr
  PC pc_1 (
    .Input(r_1_bus_out), .Clock(Primary_Clock_out), .Count(control_1_pc_inc), .Load(control_1_pc_ld),
    .Bus(control_1_pc_bus), .Bus_out(r_1_bus_out));  // open: Output
  ACC acc_1 (
    .Input(alu_1_alu_out), .Clock(Primary_Clock_out), .Load(control_1_acc_ld), .Clear(control_1_acc_clr),
    .Bus(control_1_acc_bus), .Output(acc_1_output), .Bus_out(r_1_bus_out));
  IR ir_1 (.Input(dr_1_output), .Clock(Primary_Clock_out), .Load(control_1_ir_ld), .Output(ir_1_output));
  Z_Reg z_reg_1 (.ACC_in(acc_1_output), .Clock(Primary_Clock_out), .Load(control_1_z_ld), .Z_out(z_reg_1_z_out));
  Control control_1 (
    .RAM_R_prime_W(control_1_ram_r_prime_w), .RAM_EN(control_1_ram_en), .AR_LD(control_1_ar_ld),
    .PC_BUS(control_1_pc_bus), .PC_INC(control_1_pc_inc), .PC_LD(control_1_pc_ld), .DR_BUS(control_1_dr_bus),
    .DR_LD(control_1_dr_ld), .R_BUS(control_1_r_bus), .R_LD(control_1_r_ld), .ACC_BUS(control_1_acc_bus),
    .ACC_CLR(control_1_acc_clr), .ACC_LD(control_1_acc_ld), .ALU_S(control_1_alu_s),
    .OUTR_LD(control_1_outr_ld), .Z_LD(control_1_z_ld), .IR_LD(control_1_ir_ld), .Clock(Primary_Clock_out),
    .Z_In(z_reg_1_z_out), .IR_IN(ir_1_output));  // open: T, D
  Hex_Digit_Display hex_digit_display_1 (.value(outr_1_output_2[31:28]));  // open: dp
  Hex_Digit_Display hex_digit_display_2 (.value(outr_1_output_2[23:20]));  // open: dp
  Hex_Digit_Display hex_digit_display_3 (.value(outr_1_output_2[27:24]));  // open: dp
  Hex_Digit_Display hex_digit_display_4 (.value(outr_1_output_2[15:12]));  // open: dp
  Hex_Digit_Display hex_digit_display_5 (.value(outr_1_output_2[19:16]));  // open: dp
  Hex_Digit_Display hex_digit_display_6 (.value(outr_1_output_2[11:8]));  // open: dp
  Hex_Digit_Display hex_digit_display_7 (.value(outr_1_output_2[7:4]));  // open: dp
  Hex_Digit_Display hex_digit_display_8 (.value(outr_1_output));  // open: dp
endmodule

module Decoder (
  input  [31:0] IR_In,
  output [15:0] D_Out,
  output [3:0] Debug_Instruction
);

  wire or_1_out;
  wire [3:0] or_2_out;
  wire [15:0] decoder_1_out0;

  Multiplexer #(.width(16), .enable("false")) multiplexer_1 (
    .in0(decoder_1_out0), .in1({16{1'b0}}), .out(D_Out), .sel(or_1_out));
  Decoder_part #(.select(4), .enable("false")) decoder_1 (
    .out0(decoder_1_out0[0]), .out1(decoder_1_out0[1]), .out2(decoder_1_out0[2]), .out3(decoder_1_out0[3]),
    .out4(decoder_1_out0[4]), .out5(decoder_1_out0[5]), .out6(decoder_1_out0[6]), .out7(decoder_1_out0[7]),
    .out8(decoder_1_out0[8]), .out9(decoder_1_out0[9]), .out10(decoder_1_out0[10]),
    .out11(decoder_1_out0[11]), .out12(decoder_1_out0[12]), .out13(decoder_1_out0[13]),
    .out14(decoder_1_out0[14]), .out15(decoder_1_out0[15]), .sel(IR_In[3:0]));
  or or_1 (or_1_out, or_2_out[0], or_2_out[1], or_2_out[2], or_2_out[3]);
  assign or_2_out = IR_In[7:4] | IR_In[11:8] | IR_In[15:12] | IR_In[19:16] | IR_In[23:20] | IR_In[27:24] | IR_In[31:28];  // OR_Gate or_2, 4 bits wide

  assign Debug_Instruction = IR_In[3:0];

  // Notes on the sheet:
  //   CLA7
  //   Create a D signal Generator
  //   Brandon Sandoval & Anees Alawmleh
endmodule

module Timer (
  input  Clock,
  input  Clear,
  input  Stop,
  output [7:0] T_Out
);

  wire [2:0] sequence_counter_1_seq_out;
  wire [7:0] decoder_1_out0;

  Multiplexer #(.width(8), .enable("false")) multiplexer_1 (
    .in0(decoder_1_out0), .in1({8{1'b0}}), .out(T_Out), .sel(Stop));
  Decoder_part #(.select(3), .enable("false")) decoder_1 (
    .out0(decoder_1_out0[0]), .out1(decoder_1_out0[1]), .out2(decoder_1_out0[2]), .out3(decoder_1_out0[3]),
    .out4(decoder_1_out0[4]), .out5(decoder_1_out0[5]), .out6(decoder_1_out0[6]), .out7(decoder_1_out0[7]),
    .sel(sequence_counter_1_seq_out));
  Sequence_Counter sequence_counter_1 (.Clear(Clear), .Clock(Clock), .SEQ_out(sequence_counter_1_seq_out));

  // Notes on the sheet:
  //   CLA7
  //   Create a Timer Board
  //   Brandon Sandoval & Anees Alawmleh
endmodule

module _1bit_reg (
  input  Clock,
  input  Data,
  input  Clear,
  input  Load,
  output Data_out
);

  wire and_1_out, and_2_out, not_1_out, not_2_out;

  and and_1 (and_1_out, Data, Load);
  not not_1 (not_1_out, Data);
  and and_2 (and_2_out, not_1_out, Load);
  J_K_Flip_Flop j_k_ff_1 (
    .J(and_1_out), .clk(Clock), .K(and_2_out), .Q(Data_out), .preset(1'b0), .en(not_2_out), .reset(Clear));  // open: Qn
  not not_2 (not_2_out, Clear);

  // Notes on the sheet:
  //   Brandon Sandoval
  //   OLA5
  //   10/21/2022
endmodule

module Z_Reg (
  input  Clock,
  input  [31:0] ACC_in,
  input  Load,
  output Z_out
);

  wire nor_1_out;
  wire [3:0] or_1_out;

  assign or_1_out = ACC_in[3:0] | ACC_in[7:4] | ACC_in[11:8] | ACC_in[15:12] | ACC_in[19:16] | ACC_in[23:20] | ACC_in[27:24] | ACC_in[31:28];  // OR_Gate or_1, 4 bits wide
  nor nor_1 (nor_1_out, or_1_out[0], or_1_out[1], or_1_out[2], or_1_out[3]);
  _1bit_reg Z (.Data(nor_1_out), .Clock(Clock), .Load(Load), .Clear(1'b0), .Data_out(Z_out));
endmodule

// Control Unit
module Control (
  input  Clock,
  input  [7:0] T,
  input  [31:0] IR_IN,
  input  Z_In,
  output IR_LD,
  output [3:0] D,
  output RAM_R_prime_W,
  output RAM_EN,
  output AR_LD,
  output PC_BUS,
  output PC_INC,
  output PC_LD,
  output DR_BUS,
  output DR_LD,
  output R_BUS,
  output R_LD,
  output ACC_BUS,
  output ACC_CLR,
  output ACC_LD,
  output [2:0] ALU_S,
  output OUTR_LD,
  output Z_LD
);

  wire S_data_out, S_LD_s_ld, SC_CLR_sc_clr;
  wire [7:0] timer_1_t_out;
  wire [15:0] decoder_1_d_out;

  RAM_RW RAM_RW (
    .t1(timer_1_t_out[1]), .t3(timer_1_t_out[3]), .t5(timer_1_t_out[5]), .d1(decoder_1_d_out[1]),
    .d2(decoder_1_d_out[2]), .d5(decoder_1_d_out[5]), .d6(decoder_1_d_out[6]), .z(Z_In),
    .RAM_RW(RAM_R_prime_W));
  RAM_EN u_RAM_EN (
    .t1(timer_1_t_out[1]), .t3(timer_1_t_out[3]), .t5(timer_1_t_out[5]), .t6(timer_1_t_out[6]),
    .d1(decoder_1_d_out[1]), .d2(decoder_1_d_out[2]), .d5(decoder_1_d_out[5]), .d6(decoder_1_d_out[6]),
    .z(Z_In), .RAM_EN(RAM_EN));
  AR_LD u_AR_LD (
    .t0(timer_1_t_out[0]), .t2(timer_1_t_out[2]), .t4(timer_1_t_out[4]), .clock(Clock),
    .d1(decoder_1_d_out[1]), .d2(decoder_1_d_out[2]), .AR_LD(AR_LD));
  PC_BUS u_PC_BUS (.t0(timer_1_t_out[0]), .t2(timer_1_t_out[2]), .PC_BUS(PC_BUS));
  PC_INC u_PC_INC (
    .t1(timer_1_t_out[1]), .t3(timer_1_t_out[3]), .clock(Clock), .d1(decoder_1_d_out[1]),
    .d2(decoder_1_d_out[2]), .d6(decoder_1_d_out[6]), .z(Z_In), .PC_INC(PC_INC));
  PC_LD u_PC_LD (
    .t4(timer_1_t_out[4]), .clock(Clock), .d5(decoder_1_d_out[5]), .d6(decoder_1_d_out[6]), .z(Z_In),
    .PC_LD(PC_LD));
  DR_BUS u_DR_BUS (
    .t4(timer_1_t_out[4]), .t6(timer_1_t_out[6]), .d1(decoder_1_d_out[1]), .d2(decoder_1_d_out[2]),
    .d5(decoder_1_d_out[5]), .d6(decoder_1_d_out[6]), .z(Z_In), .DR_BUS(DR_BUS));
  DR_LD u_DR_LD (
    .t1(timer_1_t_out[1]), .t3(timer_1_t_out[3]), .t5(timer_1_t_out[5]), .clock(Clock),
    .d1(decoder_1_d_out[1]), .d2(decoder_1_d_out[2]), .d5(decoder_1_d_out[5]), .d6(decoder_1_d_out[6]),
    .z(Z_In), .DR_LD(DR_LD));
  R_BUS u_R_BUS (
    .t3(timer_1_t_out[3]), .d4(decoder_1_d_out[4]), .d8(decoder_1_d_out[8]), .d9(decoder_1_d_out[9]),
    .d12(decoder_1_d_out[12]), .d13(decoder_1_d_out[13]), .R_BUS(R_BUS));
  R_LD u_R_LD (.t3(timer_1_t_out[3]), .clock(Clock), .d3(decoder_1_d_out[3]), .R_LD(R_LD));
  ACC_BUS u_ACC_BUS (
    .t3(timer_1_t_out[3]), .t5(timer_1_t_out[5]), .d3(decoder_1_d_out[3]), .d7(decoder_1_d_out[7]),
    .d2(decoder_1_d_out[2]), .ACC_BUS(ACC_BUS));
  ACC_CLR u_ACC_CLR (.t3(timer_1_t_out[3]), .d11(decoder_1_d_out[11]), .ACC_CLR(ACC_CLR));
  ACC_LD u_ACC_LD (
    .t3(timer_1_t_out[3]), .t6(timer_1_t_out[6]), .clock(Clock), .d1(decoder_1_d_out[1]),
    .d4(decoder_1_d_out[4]), .d8(decoder_1_d_out[8]), .d9(decoder_1_d_out[9]), .d10(decoder_1_d_out[10]),
    .d12(decoder_1_d_out[12]), .d13(decoder_1_d_out[13]), .d14(decoder_1_d_out[14]),
    .d15(decoder_1_d_out[15]), .ACC_LD(ACC_LD));
  ALU_SEL u_ALU_S (
    .d1(decoder_1_d_out[1]), .d4(decoder_1_d_out[4]), .d9(decoder_1_d_out[9]), .d10(decoder_1_d_out[10]),
    .d12(decoder_1_d_out[12]), .d13(decoder_1_d_out[13]), .d14(decoder_1_d_out[14]),
    .d15(decoder_1_d_out[15]), .S0(ALU_S[0]), .S1(ALU_S[1]), .S2(ALU_S[2]));
  OUTR_LD u_OUTR_LD (.t3(timer_1_t_out[3]), .clock(Clock), .d7(decoder_1_d_out[7]), .OUTR_LD(OUTR_LD));
  Z_LD u_Z_LD (.Z_LD(Z_LD));
  IR_LD u_IR_LD (.t2(timer_1_t_out[2]), .clock(Clock), .IR_LD(IR_LD));
  SC_CLR SC_CLR (
    .t4(timer_1_t_out[4]), .t5(timer_1_t_out[5]), .t7(timer_1_t_out[7]), .d1(decoder_1_d_out[1]),
    .d2(decoder_1_d_out[2]), .d5(decoder_1_d_out[5]), .d6(decoder_1_d_out[6]), .z(Z_In),
    .SC_CLR(SC_CLR_sc_clr));
  S_LD S_LD (.t3(timer_1_t_out[3]), .d0(decoder_1_d_out[0]), .clock(Clock), .S_LD(S_LD_s_ld));
  Timer timer_1 (.T_Out(timer_1_t_out), .Clock(Clock), .Clear(SC_CLR_sc_clr), .Stop(S_data_out));
  _1bit_reg S (.Data(S_LD_s_ld), .Clock(Clock), .Load(S_LD_s_ld), .Clear(1'b0), .Data_out(S_data_out));
  Decoder decoder_1 (.D_Out(decoder_1_d_out), .IR_In(IR_IN));  // open: Debug_Instruction
endmodule

// sc
module Sequence_Counter (
  input  Clock,
  input  Clear,
  output [2:0] SEQ_out
);

  wire [2:0] adder_1_out;

  Adder #(.width(3)) adder_1 (.a(SEQ_out), .b(3'b001), .out(adder_1_out));  // open: cin, cout
  Register #(.width(3)) register_1 (.D(adder_1_out), .Q(SEQ_out), .clk(Clock), .clr(Clear));  // open: en

  // Notes on the sheet:
  //   CLA6
  //   Create a Sequence Counter
  //   Brandon Sandoval & Anees Alawmleh
endmodule
