// Logisim project custom_reg.circ as structural Verilog: 12 circuits, main circuit 1bit_reg
module _1bit_reg (
  input  Clock,
  input  Data,
  input  Clear,
  input  Load,
  output Data_out
);

  wire and_1_out, and_2_out, not_1_out, not_2_out;

  and and_1 (and_1_out, Data, Load);
  not not_1 (not_1_out, Data);
  and and_2 (and_2_out, not_1_out, Load);
  J_K_Flip_Flop j_k_ff_1 (
    .J(and_1_out), .clk(Clock), .K(and_2_out), .Q(Data_out), .preset(1'b0), .en(not_2_out), .reset(Clear));  // open: Qn
  not not_2 (not_2_out, Clear);

  // Notes on the sheet:
  //   Brandon Sandoval
  //   OLA5
  //   10/21/2022
endmodule

module Register (
  input  Clock,
  input  [31:0] Data_In,
  input  Load,
  output [31:0] Data_out
);

  Register_part #(.width(32)) Reg (.D(Data_In), .en(Load), .Q(Data_out), .clk(Clock));  // open: clr

  // Notes on the sheet:
  //   OLA5
  //   Brandon Sandoval
  //   10/21/2022
endmodule

module BusRegister (
  input  Clock,
  input  [31:0] Data_In,
  input  Load,
  input  Bus,
  output [31:0] Data_out,
  output [31:0] Bus_Out
);

  Register_part #(.width(32)) Reg (.D(Data_In), .en(Load), .Q(Data_out), .clk(Clock));  // open: clr
  assign Bus_Out = Bus ? Data_out : 32'bz;  // Controlled_Buffer controlled_buffer_1

  // Notes on the sheet:
  //   Brandon Sandoval
  //   OLA5
  //   10/21/2022
endmodule

module ClearRegister (
  input  Clock,
  input  [31:0] Data_In,
  input  Load,
  input  Clear,
  input  Bus,
  output [31:0] Data_out,
  output [31:0] Bus_Out
);

  Register_part #(.width(32)) Reg (.D(Data_In), .en(Load), .Q(Data_out), .clk(Clock), .clr(Clear));
  assign Bus_Out = Bus ? Data_out : 32'bz;  // Controlled_Buffer controlled_buffer_1

  // Notes on the sheet:
  //   Brandon Sandoval
  //   OLA5
  //   10/21/2022
endmodule

module CountRegister (
  input  [31:0] Data_In,
  input  Clock,
  input  Count,
  input  Load,
  input  Bus,
  output [31:0] Data_out,
  output [31:0] Bus_Out
);

  wire or_1_out;
  wire [31:0] adder_1_out, multiplexer_1_out;

  // Probe on Data_In
  Adder #(.width(32)) adder_1 (.a(Data_out), .b(32'h1), .out(adder_1_out));  // open: cin, cout
  // Probe on multiplexer_1_out
  Multiplexer #(.width(32), .enable("false")) multiplexer_1 (
    .in0(Data_In), .in1(adder_1_out), .out(multiplexer_1_out), .sel(Count));
  Register_part #(.width(32)) Reg (.D(multiplexer_1_out), .en(or_1_out), .Q(Data_out), .clk(Clock));  // open: clr
  or or_1 (or_1_out, Count, Load);
  // Probe on Data_out
  // Probe on Data_out
  assign Bus_Out = Bus ? Data_out : 32'bz;  // Controlled_Buffer controlled_buffer_1
  // Probe on Bus_Out

  // Notes on the sheet:
  //   OLA5
  //   10/21/2022
  //   Brandon Sandoval
endmodule

module ACC (
  input  Clock,
  input  [31:0] Input,
  input  Load,
  input  Clear,
  input  Bus,
  output [31:0] Output,
  output [31:0] Bus_out
);

  ClearRegister clearregister_1 (
    .Data_In(Input), .Clock(Clock), .Load(Load), .Clear(Clear), .Bus(Bus), .Data_out(Output),
    .Bus_Out(Bus_out));

  // Notes on the sheet:
  //   OLA5
  //   10/21/2022
  //   Brandon Sandoval
  //   ACC Register: Load, Output, Bus Out, and Clear Function
endmodule

module AR (
  input  Clock,
  input  [31:0] Input,
  input  Load,
  output [31:0] Output
);

  Register register_1 (.Data_In(Input), .Clock(Clock), .Load(Load), .Data_out(Output));

  // Notes on the sheet:
  //   OLA5
  //   10/21/2022
  //   Brandon Sandoval
  //   AR: Load, Output Function
endmodule

module DR (
  input  Clock,
  input  [31:0] Input,
  input  Load,
  input  Bus,
  output [31:0] Output,
  output [31:0] Bus_out
);

  BusRegister busregister_1 (
    .Data_In(Input), .Clock(Clock), .Load(Load), .Bus(Bus), .Data_out(Output), .Bus_Out(Bus_out));

  // Notes on the sheet:
  //   OLA5
  //   Brandon Sandoval
  //   10/21/2022
  //   DR: Load, Output, Bus Out
endmodule

module IR (
  input  Clock,
  input  [31:0] Input,
  input  Load,
  output [31:0] Output
);

  Register register_1 (.Data_In(Input), .Clock(Clock), .Load(Load), .Data_out(Output));

  // Notes on the sheet:
  //   OLA5
  //   10/21/2022
  //   Brandon Sandoval
  //   IR: Load, Output Function
endmodule

module OUTR (
  input  Clock,
  input  [31:0] Input,
  input  Load,
  output [31:0] Output
);

  Register register_1 (.Data_In(Input), .Clock(Clock), .Load(Load), .Data_out(Output));

  // Notes on the sheet:
  //   OLA5
  //   10/21/2022
  //   Brandon Sandoval
  //   OUTR: Load, Output Function
endmodule

module PC (
  input  Clock,
  input  [31:0] Input,
  input  Count,
  input  Load,
  input  Bus,
  output [31:0] Output,
  output [31:0] Bus_out
);

  CountRegister countregister_1 (
    .Data_In(Input), .Clock(Clock), .Count(Count), .Load(Load), .Bus(Bus), .Data_out(Output),
    .Bus_Out(Bus_out));

  // Notes on the sheet:
  //   OLA5
  //   Brandon Sandoval
  //   10/21/2022
  //   PC: Load, Output, Bus Out, Increment
endmodule

module R (
  input  Clock,
  input  [31:0] Input,
  input  Load,
  input  Bus,
  output [31:0] Output,
  output [31:0] Bus_out
);

  BusRegister busregister_1 (
    .Data_In(Input), .Clock(Clock), .Load(Load), .Bus(Bus), .Data_out(Output), .Bus_Out(Bus_out));

  // Notes on the sheet:
  //   OLA5
  //   Brandon Sandoval
  //   10/21/2022
  //   R: Load, Output, Bus Out
endmodule
